# Fritzing sketch rmft-stage1-pin-turnouts-mcp23017 (saved by Fritzing 0.9.10b)

parts:
  Part3 = Arduino Mega 2560 (Rev3)
  3S4 = Three Aspect Signal
  3S5 = Three Aspect Signal
  3S6 = Three Aspect Signal
  8_Channel_Relay2 = 8 Channel Power Relay
  Part4 = Arduino Motor Shield (Rev3)  # not connected
  M6 = fc-51 [package=THT]
  M7 = fc-51 [package=THT]
  M8 = fc-51 [package=THT]
  M9 = fc-51 [package=THT]
  M10 = fc-51 [package=THT]
  A1 = Mcp23017 Interface Module [package=THT]  # not connected

nets:
  GND: Part3.GND, 3S4.GND, 3S5.GND, 3S6.GND, 8_Channel_Relay2.GND, M6.pin2, M7.pin2, M8.pin2, M9.pin2, M10.pin2
  5V: Part3.5V, 8_Channel_Relay2.VCC, M8.pin3, M9.pin3, M10.pin3
  N1: Part3.D22, 8_Channel_Relay2.IN1
  N2: Part3.D23, 8_Channel_Relay2.IN2
  N3: Part3.D24, M10.pin1
  N4: Part3.D25, M9.pin1
  N5: Part3.D26, M8.pin1
  N6: Part3.D27, M7.pin1
  N7: Part3.D28, M6.pin1
  N8: Part3.D30, 3S4.R
  N9: Part3.D31, 3S4.A
  N10: Part3.D32, 3S4.G
  N11: Part3.D33, 3S5.R
  N12: Part3.D34, 3S5.A
  N13: Part3.D35, 3S5.G
  N14: Part3.D36, 3S6.R
  N15: Part3.D37, 3S6.A
  N16: Part3.D38, 3S6.G
  N17: M6.pin3, M7.pin3

notes:
  SNS5_STN_TRN2_APP
  SNS4_MAIN_TRN2_APP
  SNS3_STN
  SNS2_MAIN_TRN1_EX
  SIG3_STN_EX
  SIG2_TRN2_GO
  SIG1_TRN1_APP
  SNS1_TRN1_APP

custom parts:
  Three Aspect Signal: Three aspect model railway signal.
  8 Channel Power Relay: An 8 channel power relay. The module operates at 5V.
  Mcp23017 Interface Module: The MCP23017 is capable of converting 16-bit parallel data to serial data of the IIC interface and converting each other. An internal integrated power-on reset (POR) circuit is reset to the device's default state. The two opposites become the interrupt source output. The polarity toggle register configures the GPIO input polarity.
