# Fritzing sketch rmft-stage1-pin-turnouts-mega (saved by Fritzing 0.9.10b)

parts:
  Part1 = Arduino Mega 2560 (Rev3)
  Part2 = Arduino Motor Shield (Rev3)  # not connected
  M1 = fc-51 [package=THT]
  M2 = fc-51 [package=THT]
  M3 = fc-51 [package=THT]
  M4 = fc-51 [package=THT]
  M5 = fc-51 [package=THT]
  8_Channel_Relay1 = 8 Channel Power Relay
  3S1 = Three Aspect Signal
  3S2 = Three Aspect Signal
  3S3 = Three Aspect Signal

nets:
  5V: Part1.5V, M1.pin3, M2.pin3, M3.pin3, 8_Channel_Relay1.VCC
  N1: Part1.D22, 8_Channel_Relay1.IN1
  N2: Part1.D23, 8_Channel_Relay1.IN2
  N3: Part1.D24, M1.pin1
  N4: Part1.D25, M2.pin1
  N5: Part1.D26, M3.pin1
  N6: Part1.D27, M4.pin1
  N7: Part1.D28, M5.pin1
  N8: Part1.D30, 3S1.R
  N9: Part1.D31, 3S1.A
  N10: Part1.D32, 3S1.G
  N11: Part1.D33, 3S2.R
  N12: Part1.D34, 3S2.A
  N13: Part1.D35, 3S2.G
  N14: Part1.D36, 3S3.R
  N15: Part1.D37, 3S3.A
  N16: Part1.D38, 3S3.G
  GND: Part1.GND, M1.pin2, M2.pin2, M3.pin2, M4.pin2, M5.pin2, 8_Channel_Relay1.GND, 3S1.GND, 3S2.GND, 3S3.GND
  N17: M4.pin3, M5.pin3

notes:
  SNS1_TRN1_APP
  SNS2_MAIN_TRN1_EX
  SNS3_STN
  SNS4_MAIN_TRN2_APP
  SNS5_STN_TRN2_APP
  SIG1_TRN1_APP
  SIG2_TRN2_GO
  SIG3_STN_EX

custom parts:
  8 Channel Power Relay: An 8 channel power relay. The module operates at 5V.
  Three Aspect Signal: Three aspect model railway signal.
